# Fritzing sketch 3rd Rev (saved by Fritzing 0.9.3b)
breadboards: 1

parts:
  Part1 = Arduino Nano (Rev3.0)
  V1 = DC Power [voltage=5]
  J1 = female pin header, 5 pins [form="♀ (female)"]
  J2 = female pin header, 5 pins [form="♀ (female)"]
  J3 = female pin header, 5 pins [form="♀ (female)"]
  J4 = female pin header, 5 pins [form="♀ (female)"]
  R1 = Resistor [tolerance=±5% resistance=150 package=THT]
  LED1 = LED - 5mm [color="Red (633nm)" package="5 mm [THT]"]
  R2 = Resistor [tolerance=±5% resistance=220 package=THT]
  U1 = WS2812 RGB LED strip
  M1 = fc-51 [package=THT]
  U2 = WS2812 RGB LED strip
  J5 = female pin header, 5 pins [form="♀ (female)"]
  M2 = fc-51 [package=THT]

nets:
  GND: Part1.GND, V1.V-, J1.pin2, J2.pin2, J3.pin2, J4.pin2, LED1.cathode, U1.GND, M1.pin2
  N1: Part1.D2, R1.Pin_0
  N2: Part1.D3, J1.pin5
  N3: Part1.D4, J2.pin5
  N4: Part1.D5, M1.pin1
  N5: Part1.D6, J3.pin5
  N6: Part1.D7, R2.Pin_0
  N7: Part1.D8, J4.pin5
  N8: Part1.VIN, V1.V+
  5V: Part1.5V, J1.pin1, J2.pin1, J3.pin1, J4.pin1, U1.VCC, M1.pin3
  N9: J1.pin3, R2.Pin_1
  N10: J1.pin4, J2.pin3
  N11: J2.pin4, U1.DIN
  N12: J3.pin3, U1.DOUT
  N13: J3.pin4, J4.pin3
  N14: R1.Pin_1, LED1.anode
  N15: U2.GND, J5.pin2, M2.pin2
  N16: U2.VCC#1, J5.pin1, M2.pin3
  N17: U2.DIN, U2.VCC#5, J5.pin3
  N18: U2.DOUT, J5.pin4

notes:
  Single Hex
  Main Hex

custom parts:
  WS2812 RGB LED strip: WS2812 strip
